// Logisim project jws146_lab6.circ as structural Verilog: 1 circuit, main circuit main
module main (
);

  wire button_1_out, CLK, CMD_T_out, decoder_1_out0, decoder_1_out1, decoder_1_out2, decoder_1_out3,
       decoder_1_out4, decoder_1_out5, decoder_1_out6, decoder_1_out7, decoder_1_out8, decoder_1_out9,
       decoder_1_out10, decoder_1_out11, decoder_1_out12, decoder_1_out13, decoder_1_out14, decoder_1_out15;
  wire [3:0] adder_1_out, count;

  Clock CMD_T (.out(CMD_T_out));
  Button button_1 (.out(button_1_out));
  LED led_1 (.in(decoder_1_out0));
  LED led_2 (.in(decoder_1_out1));
  or or_1 (CLK, CMD_T_out, button_1_out);
  LED led_3 (.in(decoder_1_out5));
  LED led_4 (.in(decoder_1_out2));
  LED led_5 (.in(decoder_1_out3));
  LED led_6 (.in(decoder_1_out4));
  Decoder #(.select(4)) decoder_1 (
    .out0(decoder_1_out0), .out1(decoder_1_out1), .out2(decoder_1_out2), .out3(decoder_1_out3),
    .out4(decoder_1_out4), .out5(decoder_1_out5), .out6(decoder_1_out6), .out7(decoder_1_out7),
    .out8(decoder_1_out8), .out9(decoder_1_out9), .out10(decoder_1_out10), .out11(decoder_1_out11),
    .out12(decoder_1_out12), .out13(decoder_1_out13), .out14(decoder_1_out14), .out15(decoder_1_out15),
    .sel(count));  // open: en
  Register #(.width(4)) register_1 (.D(adder_1_out), .Q(count), .clk(CLK));  // open: en, clr
  LED led_7 (.in(decoder_1_out9));
  LED V (.in(decoder_1_out7));
  LED led_8 (.in(decoder_1_out6));
  LED led_9 (.in(decoder_1_out8));
  LED led_10 (.in(decoder_1_out12));
  LED led_11 (.in(decoder_1_out10));
  LED led_12 (.in(decoder_1_out11));
  LED led_13 (.in(decoder_1_out13));
  Adder #(.width(4)) adder_1 (.a(count), .b(4'b0001), .out(adder_1_out));  // open: cin, cout
  LED led_14 (.in(decoder_1_out14));
  LED led_15 (.in(decoder_1_out15));

  // Notes on the sheet:
  //   connect clock signal to registers
  //   increments every full clock cycle
  //   CMD + R to reset circuit
endmodule
